# Fritzing sketch Raspberry_lcd (saved by Fritzing 0.8.7b)
breadboards: 1

parts:
  Raspberry_Pi_1 = Raspberry Pi 3
  U1 = LCD-16X2 [package=lcd-16x2]

nets:
  N1: Raspberry_Pi_1.GIPO4, U1.RS
  N2: Raspberry_Pi_1.GIPO17, U1.E
  N3: Raspberry_Pi_1.GIPO22, U1.DB5
  GND: Raspberry_Pi_1.GND, U1.VSS, U1.VO, U1.R_W, U1.K
  N4: Raspberry_Pi_1.GIPO24, U1.DB7
  N5: Raspberry_Pi_1.GIPO23, U1.DB6
  N6: Raspberry_Pi_1.GIPO18, U1.DB4
  5V: Raspberry_Pi_1.5V, U1.VDD, U1.A
