# Fritzing sketch Raspberry_led (saved by Fritzing 0.8.7b)
breadboards: 1

parts:
  Raspberry_Pi_1 = Raspberry Pi 3
  R1 = Resistor [tolerance=±5% resistance=220 package="0603 [SMD]"]
  LED1 = smd LED [color="Red (633nm)" package="1206 [SMD]"]

nets:
  N1: Raspberry_Pi_1.GND, LED1.cathode
  N2: Raspberry_Pi_1.GIPO18, R1.Pin_1
  N3: R1.Pin_0, LED1.anode
