# Fritzing sketch Raspberry_led_button (saved by Fritzing 0.8.7b)
breadboards: 1

parts:
  Raspberry_Pi_1 = Raspberry Pi 3
  R1 = Resistor [tolerance=±5% resistance=220 package="0603 [SMD]"]
  LED1 = smd LED [color="Red (633nm)" package="1206 [SMD]"]
  S1 = Pushbutton [package="[THT]"]

nets:
  N1: Raspberry_Pi_1.GPIO2, S1.Pin_3, S1.Pin_4
  N2: Raspberry_Pi_1.GND, LED1.cathode, S1.Pin_1, S1.Pin_2
  N3: Raspberry_Pi_1.GIPO18, R1.Pin_1
  N4: R1.Pin_0, LED1.anode
